# Fritzing sketch Fritzing (saved by Fritzing 0.9.9b)
breadboards: 1

parts:
  MCU1 = Raspberry Pi Zero
  U1 = MAX6675 [package=so08]
  U2 = MAX6675 [package=so08]
  U4 = RELAY-SOLIDSTATE [package=relay-s108t02]  # not connected
  U3 = RELAY-SOLIDSTATE [package=relay-s108t02]

nets:
  VDD: MCU1.pin_1, MCU1.pin_17, U1.VDD, U2.VDD
  N1: MCU1.pin_4, U3.1
  VSS: MCU1.pin_6, MCU1.pin_9, MCU1.pin_39, U1.VSS, U2.VSS, U3.2
  N2: MCU1.pin_8, U3.3
  N3: MCU1.pin_10, U3.4
  N4: MCU1.pin_21, U1.MISO, U2.MISO
  N5: MCU1.pin_23, U1.SCK, U2.SCK
  N6: MCU1.pin_24, U1.CS
  N7: MCU1.pin_26, U2.CS

custom parts:
  RELAY-SOLIDSTATE: SPST SS relay
